// Logisim project 4 bit adder on logisim.circ as structural Verilog: 1 circuit, main circuit main
module main (
  input  I0,
  input  I1,
  input  I2,
  input  I3,
  output S0,
  output S1,
  output S2,
  output S3
);

  wire and_1_out, and_2_out, and_3_out, and_4_out, and_5_out, or_1_out, or_2_out, xor_2_out, xor_3_out,
       xor_4_out;

  xor xor_1 (S0, 1'b1, I0);
  and and_1 (and_1_out, 1'b1, I0);
  xor xor_2 (xor_2_out, 1'b1, I1);
  and and_2 (and_2_out, 1'b1, I1);
  xor xor_3 (xor_3_out, 1'b0, I2);
  and and_3 (and_3_out, 1'b0, I2);
  xor xor_4 (xor_4_out, 1'b0, I3);
  xor xor_5 (S1, and_1_out, xor_2_out);
  and and_4 (and_4_out, xor_2_out, and_1_out);
  or or_1 (or_1_out, and_4_out, and_2_out);
  xor xor_6 (S2, or_1_out, xor_3_out);
  and and_5 (and_5_out, or_1_out, xor_3_out);
  or or_2 (or_2_out, and_5_out, and_3_out);
  xor xor_7 (S3, or_2_out, xor_4_out);
endmodule
