// Logisim project 4 bit comparator.circ as structural Verilog: 1 circuit, main circuit main
module main (
  input  B3,
  input  B2,
  input  B1,
  input  B0,
  output A___4
);

  wire AND1_out, AND2_out, AND3_out, AND4_out, not_1_out, not_2_out, not_3_out, not_4_out, XOR1_out,
       XOR2_out, XOR3_out;

  not not_1 (not_1_out, 1'b0);
  not not_2 (not_2_out, 1'b1);
  not not_3 (not_3_out, 1'b0);
  not not_4 (not_4_out, 1'b0);
  nor XOR1 (XOR1_out, 1'b0, B3);
  xnor XOR2 (XOR2_out, B2, 1'b1);
  xnor XOR3 (XOR3_out, B1, 1'b0);
  and AND1 (AND1_out, not_1_out, B3);
  and AND2 (AND2_out, XOR1_out, not_2_out, B2);
  and AND3 (AND3_out, XOR1_out, XOR2_out, not_3_out, B1);
  and AND4 (AND4_out, B0, XOR1_out, XOR2_out, XOR3_out, not_4_out);
  or XOR4 (A___4, AND1_out, AND2_out, AND3_out, AND4_out);
endmodule
