// Logisim project Comparative Adder.circ as structural Verilog: 1 circuit, main circuit main
module main (
  input  I0,
  input  I1,
  input  I2,
  input  I3,
  output O0,
  output O1,
  output O2,
  output O3
);

  wire main_1_out_5, main_1_out_6, main_1_out_7, main_1_out_8, main_2_a___4;

  _4_bit_adder_on_logisim_main main_1 (
    .I0(I0), .I1(I1), .I2(I2), .I3(I3), .out_5(main_1_out_5), .out_6(main_1_out_6), .out_7(main_1_out_7),
    .out_8(main_1_out_8));
  _4_bit_comparator_main main_2 (.B3(I3), .B2(I2), .B1(I1), .B0(I0), .A___4(main_2_a___4));
  Multiplexer #(.enable("false")) multiplexer_1 (.in0(I0), .in1(main_1_out_5), .out(O0), .sel(main_2_a___4));
  Multiplexer #(.enable("false")) multiplexer_2 (.in0(I1), .in1(main_1_out_6), .out(O1), .sel(main_2_a___4));
  Multiplexer #(.enable("false")) multiplexer_3 (.in0(I2), .in1(main_1_out_7), .out(O2), .sel(main_2_a___4));
  Multiplexer #(.enable("false")) multiplexer_4 (.in0(I3), .in1(main_1_out_8), .out(O3), .sel(main_2_a___4));
endmodule
