// Logisim project DoubleDabble.circ as structural Verilog: 1 circuit, main circuit main
module main (
  input  B0,
  input  B1,
  input  B2,
  input  B3,
  input  B4,
  input  B5,
  input  B6,
  input  B7,
  input  B8,
  input  B9,
  input  B10,
  input  B11,
  input  B12,
  input  B13,
  input  B14,
  input  B15,
  output out_17,
  output out_18,
  output out_19,
  output out_20,
  output out_21,
  output out_22,
  output out_23,
  output out_24,
  output out_25,
  output out_26,
  output out_27,
  output out_28,
  output out_29,
  output out_30,
  output out_31,
  output out_32
);

  wire CA1_o0, CA1_o1, CA1_o2, CA1_o3, CA2_o0, CA2_o1, CA2_o2, CA2_o3, CA3_o0, CA3_o1, CA3_o2, CA3_o3,
       CA4_o0, CA4_o1, CA4_o2, CA4_o3, CA5_o0, CA5_o1, CA5_o2, CA5_o3, CA6_o0, CA6_o1, CA6_o2, CA6_o3,
       CA7_o0, CA7_o1, CA7_o2, CA7_o3, CA8_o0, CA8_o1, CA8_o2, CA8_o3, CA9_o0, CA9_o1, CA9_o2, CA9_o3,
       CA10_o0, CA10_o1, CA10_o2, CA10_o3, CA11_o0, CA11_o1, CA11_o2, CA11_o3, CA12_o0, CA12_o1, CA12_o2,
       CA12_o3, CA13_o0, CA13_o1, CA13_o2, CA13_o3, CA14_o0, CA14_o1, CA14_o2, CA14_o3, CA15_o0, CA15_o1,
       CA15_o2, CA15_o3, CA16_o0, CA16_o1, CA16_o2, CA16_o3, CA17_o0, CA17_o1, CA17_o2, CA17_o3, CA18_o0,
       CA18_o1, CA18_o2, CA18_o3, CA19_o0, CA19_o1, CA19_o2, CA19_o3, CA20_o0, CA20_o1, CA20_o2, CA20_o3,
       CA21_o0, CA21_o1, CA21_o2, CA21_o3, CA22_o0, CA22_o1, CA22_o2, CA22_o3, CA23_o0, CA23_o1, CA23_o2,
       CA23_o3, CA24_o0, CA24_o1, CA24_o2, CA24_o3, CA25_o0, CA25_o1, CA25_o2, CA25_o3, CA26_o0, CA26_o1,
       CA26_o2, CA26_o3, CA27_o0, CA27_o1, CA27_o2, CA27_o3, CA28_o0, CA28_o1, CA28_o2, CA28_o3, CA29_o0,
       CA29_o1, CA29_o2, CA29_o3, CA30_o0, CA30_o1, CA30_o2, CA30_o3;

  Comparative_Adder_main CA1 (
    .I0(B13), .I1(B14), .I2(B15), .I3(1'b0), .O0(CA1_o0), .O1(CA1_o1), .O2(CA1_o2), .O3(CA1_o3));
  Comparative_Adder_main CA3 (
    .I0(B11), .I1(CA2_o0), .I2(CA2_o1), .I3(CA2_o2), .O0(CA3_o0), .O1(CA3_o1), .O2(CA3_o2), .O3(CA3_o3));
  Comparative_Adder_main CA2 (
    .I0(B12), .I1(CA1_o0), .I2(CA1_o1), .I3(CA1_o2), .O0(CA2_o0), .O1(CA2_o1), .O2(CA2_o2), .O3(CA2_o3));
  Comparative_Adder_main CA7 (
    .I0(B9), .I1(CA5_o0), .I2(CA5_o1), .I3(CA5_o2), .O0(CA7_o0), .O1(CA7_o1), .O2(CA7_o2), .O3(CA7_o3));
  Comparative_Adder_main CA5 (
    .I0(B10), .I1(CA3_o0), .I2(CA3_o1), .I3(CA3_o2), .O0(CA5_o0), .O1(CA5_o1), .O2(CA5_o2), .O3(CA5_o3));
  Comparative_Adder_main CA6 (
    .I0(CA5_o3), .I1(CA4_o0), .I2(CA4_o1), .I3(CA4_o2), .O0(CA6_o0), .O1(CA6_o1), .O2(CA6_o2), .O3(CA6_o3));
  Comparative_Adder_main CA4 (
    .I0(CA3_o3), .I1(CA2_o3), .I2(CA1_o3), .I3(1'b0), .O0(CA4_o0), .O1(CA4_o1), .O2(CA4_o2), .O3(CA4_o3));
  Comparative_Adder_main CA9 (
    .I0(B8), .I1(CA7_o0), .I2(CA7_o1), .I3(CA7_o2), .O0(CA9_o0), .O1(CA9_o1), .O2(CA9_o2), .O3(CA9_o3));
  Comparative_Adder_main CA8 (
    .I0(CA7_o3), .I1(CA6_o0), .I2(CA6_o1), .I3(CA6_o2), .O0(CA8_o0), .O1(CA8_o1), .O2(CA8_o2), .O3(CA8_o3));
  Comparative_Adder_main CA15 (
    .I0(B6), .I1(CA12_o0), .I2(CA12_o1), .I3(CA12_o2), .O0(CA15_o0), .O1(CA15_o1), .O2(CA15_o2), .O3(CA15_o3));
  Comparative_Adder_main CA12 (
    .I0(B7), .I1(CA9_o0), .I2(CA9_o1), .I3(CA9_o2), .O0(CA12_o0), .O1(CA12_o1), .O2(CA12_o2), .O3(CA12_o3));
  Comparative_Adder_main CA14 (
    .I0(CA12_o3), .I1(CA11_o0), .I2(CA11_o1), .I3(CA11_o2), .O0(CA14_o0), .O1(CA14_o1), .O2(CA14_o2),
    .O3(CA14_o3));
  Comparative_Adder_main CA11 (
    .I0(CA9_o3), .I1(CA8_o0), .I2(CA8_o1), .I3(CA8_o2), .O0(CA11_o0), .O1(CA11_o1), .O2(CA11_o2), .O3(CA11_o3));
  Comparative_Adder_main CA13 (
    .I0(CA11_o3), .I1(CA10_o0), .I2(CA10_o1), .I3(CA10_o2), .O0(CA13_o0), .O1(CA13_o1), .O2(CA13_o2),
    .O3(CA13_o3));
  Comparative_Adder_main CA10 (
    .I0(CA8_o3), .I1(CA6_o3), .I2(CA4_o3), .I3(1'b0), .O0(CA10_o0), .O1(CA10_o1), .O2(CA10_o2), .O3(CA10_o3));
  Comparative_Adder_main CA18 (
    .I0(B5), .I1(CA15_o0), .I2(CA15_o1), .I3(CA15_o2), .O0(CA18_o0), .O1(CA18_o1), .O2(CA18_o2), .O3(CA18_o3));
  Comparative_Adder_main CA17 (
    .I0(CA15_o3), .I1(CA14_o0), .I2(CA14_o1), .I3(CA14_o2), .O0(CA17_o0), .O1(CA17_o1), .O2(CA17_o2),
    .O3(CA17_o3));
  Comparative_Adder_main CA16 (
    .I0(CA14_o3), .I1(CA13_o0), .I2(CA13_o1), .I3(CA13_o2), .O0(CA16_o0), .O1(CA16_o1), .O2(CA16_o2),
    .O3(CA16_o3));
  Comparative_Adder_main CA22 (
    .I0(B4), .I1(CA18_o0), .I2(CA18_o1), .I3(CA18_o2), .O0(CA22_o0), .O1(CA22_o1), .O2(CA22_o2), .O3(CA22_o3));
  Comparative_Adder_main CA21 (
    .I0(CA18_o3), .I1(CA17_o0), .I2(CA17_o1), .I3(CA17_o2), .O0(CA21_o0), .O1(CA21_o1), .O2(CA21_o2),
    .O3(CA21_o3));
  Comparative_Adder_main CA20 (
    .I0(CA17_o3), .I1(CA16_o0), .I2(CA16_o1), .I3(CA16_o2), .O0(CA20_o0), .O1(CA20_o1), .O2(CA20_o2),
    .O3(CA20_o3));
  Comparative_Adder_main CA19 (
    .I0(CA16_o3), .I1(CA13_o3), .I2(CA10_o3), .I3(1'b0), .O0(CA19_o0), .O1(CA19_o1), .O2(CA19_o2),
    .O3(CA19_o3));
  Comparative_Adder_main CA26 (
    .I0(B3), .I1(CA22_o0), .I2(CA22_o1), .I3(CA22_o2), .O0(CA26_o0), .O1(CA26_o1), .O2(CA26_o2), .O3(CA26_o3));
  Comparative_Adder_main CA25 (
    .I0(CA22_o3), .I1(CA21_o0), .I2(CA21_o1), .I3(CA21_o2), .O0(CA25_o0), .O1(CA25_o1), .O2(CA25_o2),
    .O3(CA25_o3));
  Comparative_Adder_main CA24 (
    .I0(CA21_o3), .I1(CA20_o0), .I2(CA20_o1), .I3(CA20_o2), .O0(CA24_o0), .O1(CA24_o1), .O2(CA24_o2),
    .O3(CA24_o3));
  Comparative_Adder_main CA23 (
    .I0(CA20_o3), .I1(CA19_o0), .I2(CA19_o1), .I3(CA19_o2), .O0(CA23_o0), .O1(CA23_o1), .O2(CA23_o2),
    .O3(CA23_o3));
  Comparative_Adder_main CA30 (
    .I0(B2), .I1(CA26_o0), .I2(CA26_o1), .I3(CA26_o2), .O0(CA30_o0), .O1(CA30_o1), .O2(CA30_o2), .O3(CA30_o3));
  Comparative_Adder_main CA29 (
    .I0(CA26_o3), .I1(CA25_o0), .I2(CA25_o1), .I3(CA25_o2), .O0(CA29_o0), .O1(CA29_o1), .O2(CA29_o2),
    .O3(CA29_o3));
  Comparative_Adder_main CA28 (
    .I0(CA25_o3), .I1(CA24_o0), .I2(CA24_o1), .I3(CA24_o2), .O0(CA28_o0), .O1(CA28_o1), .O2(CA28_o2),
    .O3(CA28_o3));
  Comparative_Adder_main CA27 (
    .I0(CA24_o3), .I1(CA23_o0), .I2(CA23_o1), .I3(CA23_o2), .O0(CA27_o0), .O1(CA27_o1), .O2(CA27_o2),
    .O3(CA27_o3));
  Comparative_Adder_main CA35 (
    .I0(B1), .I1(CA30_o0), .I2(CA30_o1), .I3(CA30_o2), .O0(out_18), .O1(out_19), .O2(out_20), .O3(out_21));
  Comparative_Adder_main CA34 (
    .I0(CA30_o3), .I1(CA29_o0), .I2(CA29_o1), .I3(CA29_o2), .O0(out_22), .O1(out_23), .O2(out_24), .O3(out_25));
  Comparative_Adder_main CA33 (
    .I0(CA29_o3), .I1(CA28_o0), .I2(CA28_o1), .I3(CA28_o2), .O0(out_26), .O1(out_27), .O2(out_28), .O3(out_29));
  Comparative_Adder_main CA32 (
    .I0(CA28_o3), .I1(CA27_o0), .I2(CA27_o1), .I3(CA27_o2), .O0(out_30), .O1(out_31), .O2(out_32));  // open: O3
  Comparative_Adder_main CA31 (.I0(CA27_o3), .I1(CA23_o3), .I2(CA19_o3), .I3(1'b0));  // open: O0, O1, O2, O3

  assign out_17 = B0;
endmodule
